// Logisim project project-1.circ as structural Verilog: 5 circuits, main circuit main
module main (
  input  in_1,
  input  in_2,
  input  in_3,
  input  in_4,
  input  in_5,
  input  in_6,
  input  in_7,
  input  in_8,
  input  in_9,
  input  in_10,
  input  in_11,
  input  in_12
);

  wire Clock;
  wire [31:0] A_dout, alu_32_1_out, B_dout, controlled_buffer_1_out, IR_dout, MAR_dout, PC_dout, undriven,
       undriven_2, undriven_3;

  Clock clock_1 (.out(Clock));
  myRegister PC (.Din(undriven), .LdREG(in_1), .Clock(Clock), .Dout(PC_dout));
  assign controlled_buffer_1_out = in_2 ? PC_dout : 32'bz;  // Controlled_Buffer controlled_buffer_1
  myRegister A (.Din(undriven), .LdREG(in_4), .Clock(Clock), .Dout(A_dout));
  ALU_32 alu_32_1 (.A(A_dout), .B(B_dout), .out(alu_32_1_out), .func(3'b111));  // open: out_5, out_6, out_7, out_4
  assign controlled_buffer_1_out = in_3 ? alu_32_1_out : 32'bz;  // Controlled_Buffer controlled_buffer_2
  myRegister B (.Din(undriven), .LdREG(in_5), .Clock(Clock), .Dout(B_dout));
  Register_File register_file_1 (.Din(undriven), .WrREG(in_7), .regno(5'b00001), .Clock(Clock), .Dout(undriven_2));
  assign controlled_buffer_1_out = in_6 ? undriven_2 : 32'bz;  // Controlled_Buffer controlled_buffer_3
  myRegister MAR (.Din(undriven), .LdREG(in_8), .Clock(Clock), .Dout(MAR_dout));
  Memory memory_1 (.Din(undriven), .WrMEM(in_9), .addr(MAR_dout), .Clock(Clock), .Dout(undriven_3));
  assign controlled_buffer_1_out = in_10 ? undriven_3 : 32'bz;  // Controlled_Buffer controlled_buffer_4
  myRegister IR (.Din(undriven), .LdREG(in_11), .Clock(Clock), .Dout(IR_dout));
  Controlled_Buffer #(.width(32)) controlled_buffer_5 (.out(controlled_buffer_1_out), .en(in_12));  // open: in

  // Other names for the same wires on the sheet: DrALU = in_3; DrMEM = in_10; DrOFF = in_12; DrPC = in_2;
  //   DrREG = in_6; LdA = in_4; LdB = in_5; LdIR = in_11; LdMAR = in_8; LdPC = in_1; WrMEM = in_9; WrREG = in_7
endmodule

// ALU
module ALU_32 (
  input  [2:0] func,
  input  [31:0] A,
  input  [31:0] B,
  output [31:0] out_4,
  output [31:0] out_5,
  output [31:0] out_6,
  output [2:0] out_7,
  output [31:0] out
);

  wire [31:0] adder_1_out, adder_2_out, multiplier_1_out, or_1_out, shifter_1_out, shifter_2_out,
       subtractor_1_out;

  Adder #(.width(32)) adder_1 (.a(A), .b(B), .out(adder_1_out));  // open: cin, cout
  Adder #(.width(32)) adder_2 (.a(A), .b(32'h1), .out(adder_2_out));  // open: cin, cout
  Subtractor #(.width(32)) subtractor_1 (.a(A), .b(B), .out(subtractor_1_out));  // open: bin, bout
  Multiplier #(.width(32)) multiplier_1 (.a(A), .b(B), .out(multiplier_1_out));  // open: cin, cout
  Shifter #(.width(32)) shifter_1 (.in(A), .\dist (B[4:0]), .out(shifter_1_out));
  Shifter #(.width(32), .shift("lr")) shifter_2 (.in(A), .\dist (B[4:0]), .out(shifter_2_out));
  assign out_6 = A & B;  // AND_Gate and_1, 32 bits wide
  assign or_1_out = A | B;  // OR_Gate or_1, 32 bits wide
  Multiplexer #(.select(3), .width(32), .enable("false")) multiplexer_1 (
    .in0(adder_1_out), .in1(adder_2_out), .in2(subtractor_1_out), .in3(multiplier_1_out),
    .in4(shifter_1_out), .in5(shifter_2_out), .in6(out_6), .in7(or_1_out), .out(out), .sel(func));

  assign out_4 = A;
  assign out_5 = B;
  assign out_7 = func;

  // Notes on the sheet:
  //   Adder-32
  //   A + 1
  //   A - B
  //   Mult
  //   Shift Left
  //   Shift Right
  //   AND-32
  //   OR-32
endmodule

// Register File \n 32 x 32 bits
module Register_File (
  input  [31:0] Din,
  input  WrREG,
  input  [4:0] regno,
  input  Clock,
  input  [31:0] Dout
);

  wire not_1_out;

  assign Dout = WrREG ? Din : 32'bz;  // Controlled_Buffer controlled_buffer_1
  not not_1 (not_1_out, WrREG);
  RAM #(.addrWidth(5), .dataWidth(32)) ram_1 (
    .addr(regno), .data(Dout), .sel(Clock), .ld(not_1_out));  // open: clk, clr
endmodule

// Reg
module myRegister (
  input  [31:0] Din,
  input  LdREG,
  input  Clock,
  output [31:0] Dout
);

  Register #(.width(32)) register_1 (.D(Din), .en(LdREG), .Q(Dout), .clk(Clock));  // open: clr
endmodule

// Memory\n2^24 x 32 bits
module Memory (
  input  [31:0] Din,
  input  WrMEM,
  input  [31:0] addr,
  input  Clock,
  input  [31:0] Dout
);

  wire not_1_out;

  assign Dout = WrMEM ? Din : 32'bz;  // Controlled_Buffer controlled_buffer_1
  not not_1 (not_1_out, WrMEM);
  RAM #(.addrWidth(24), .dataWidth(32)) ram_1 (
    .addr(addr[23:0]), .data(Dout), .sel(Clock), .ld(not_1_out));  // open: clk, clr
endmodule
