// Logisim project prj-3.circ as structural Verilog: 8 circuits, main circuit main
module main (
  output [31:0] out_1
);

  wire chk_z, Clock, Clr, undriven;
  wire [1:0] undriven_2;
  wire [3:0] D_Read_1, D_Read_2, Dest_Reg, fetch_buffer_1_rd_out, fetch_buffer_1_rs_b_out,
       id_rr_buffer_1_dest_out, multiplexer_3_out;
  wire [5:0] fetch_buffer_1_opcode_out, id_rr_buffer_1_opcode_out;
  wire [15:0] fetch_buffer_1_offset_out;
  wire [31:0] alu_main_1_alu_out, BEQ_PC, bit_extender_1_out, controlled_buffer_1_out, D_Out_1, D_Out_2,
       dual_ported_register_file_1_out1, dual_ported_register_file_1_out2, fetch_buffer_1_pc_out,
       id_rr_buffer_1_data_r2_out, id_rr_buffer_1_pc_out, instruction_memory_1_dout, JALR_PC,
       multiplexer_1_out, multiplexer_4_out, multiplexer_5_out, multiplexer_6_out, Offset, PC_1, pc_1_dout,
       ToWrite;

  Multiplexer #(.select(2), .width(32)) multiplexer_1 (
    .in0(PC_1), .in1(BEQ_PC), .in2(JALR_PC), .out(multiplexer_1_out), .sel({chk_z, 1'b0}));  // open: in3, en
  PC u_pc_1 (.Din(multiplexer_1_out), .Dout(pc_1_dout), .Clk(Clock), .Clear_PC(Clr));
  Counter #(.width(32), .max('hffffffff)) counter_1 (
    .load(1'b0), .count(1'b1), .Q(out_1), .clk(Clock), .clr(Clr));  // open: D, carry
  Clock clock_1 (.out(Clock));
  Button button_1 (.out(Clr));
  _1 u_1_1 (.Din(pc_1_dout), .Dout(PC_1));
  Instruction_Memory instruction_memory_1 (
    .Din(pc_1_dout), .Dout(instruction_memory_1_dout), .Clk(Clock));  // open: Clear_IR
  Fetch_Buffer fetch_buffer_1 (
    .Offset_In(instruction_memory_1_dout[15:0]), .Rs_B_In(instruction_memory_1_dout[15:12]),
    .Rs_A_In(instruction_memory_1_dout[19:16]), .Rd_In(instruction_memory_1_dout[23:20]),
    .OpCode_In(instruction_memory_1_dout[31:26]), .PC_In(PC_1), .Clk_FBuff(Clock),
    .Offset_Out(fetch_buffer_1_offset_out), .Rs_B_Out(fetch_buffer_1_rs_b_out), .Rs_A_Out(D_Read_2),
    .Rd_Out(fetch_buffer_1_rd_out), .Opcode_Out(fetch_buffer_1_opcode_out), .PC_Out(fetch_buffer_1_pc_out));
  assign bit_extender_1_out = {{16{1'b0}}, fetch_buffer_1_offset_out};  // Bit_Extender bit_extender_1
  Multiplexer #(.width(4), .enable("false")) multiplexer_2 (
    .in0(fetch_buffer_1_rs_b_out), .in1(fetch_buffer_1_rd_out), .out(D_Read_1), .sel(1'b0));
  Multiplexer #(.width(4), .enable("false")) multiplexer_3 (
    .in0(D_Read_2), .in1(fetch_buffer_1_rd_out), .out(multiplexer_3_out), .sel(1'b1));
  ROM #(.addrWidth(6)) rom_1 (.addr(fetch_buffer_1_opcode_out));  // open: data, sel
  Dual_Ported_Register_File dual_ported_register_file_1 (
    .CLK(Clock), .WrREGNO(Dest_Reg), .RdREGNO1(D_Read_1), .RdREGNO2(D_Read_2), .INPUT(ToWrite),
    .OUT1(dual_ported_register_file_1_out1), .OUT2(dual_ported_register_file_1_out2));  // open: WrEN
  Multiplexer #(.width(32), .enable("false")) multiplexer_4 (
    .in0(dual_ported_register_file_1_out1), .in1(D_Out_1), .out(multiplexer_4_out), .sel(1'b0));
  Multiplexer #(.width(32), .enable("false")) multiplexer_5 (
    .in0(dual_ported_register_file_1_out2), .in1(D_Out_2), .out(multiplexer_5_out), .sel(1'b0));
  ID_RR_Buffer id_rr_buffer_1 (
    .Offset_In(bit_extender_1_out), .Data_R1_In(multiplexer_4_out), .Data_R2_In(multiplexer_5_out),
    .Dest_In(multiplexer_3_out), .OpCode_In(fetch_buffer_1_opcode_out), .PC_In(fetch_buffer_1_pc_out),
    .Clk_FBuff(Clock), .Offset_Out(Offset), .Data_R1_Out(JALR_PC), .Data_R2_Out(id_rr_buffer_1_data_r2_out),
    .Dest_Out(id_rr_buffer_1_dest_out), .Opcode_Out(id_rr_buffer_1_opcode_out), .PC_Out(id_rr_buffer_1_pc_out));
  Multiplexer #(.width(32), .enable("false")) multiplexer_6 (
    .in0(JALR_PC), .in1(Offset), .out(multiplexer_6_out), .sel(undriven));
  Adder #(.width(32)) adder_1 (.a(Offset), .b(id_rr_buffer_1_pc_out), .out(BEQ_PC));  // open: cin, cout
  ALU_Main alu_main_1 (
    .FUNC(undriven_2), .A_In(multiplexer_6_out), .B_In(id_rr_buffer_1_data_r2_out),
    .ALU_out(alu_main_1_alu_out));
  Controlled_Buffer #(.width(32)) controlled_buffer_1 (
    .in(alu_main_1_alu_out), .out(controlled_buffer_1_out));  // open: en
  _0 u_0_1 (.Din(controlled_buffer_1_out), .Dout(chk_z));
  ROM #(.addrWidth(6)) rom_2 (.addr(id_rr_buffer_1_opcode_out));  // open: data, sel
  EX_Buffer ex_buffer_1 (
    .Rx_In(JALR_PC), .ALU_In(alu_main_1_alu_out), .Dest_In(id_rr_buffer_1_dest_out),
    .OpCode_In(id_rr_buffer_1_opcode_out), .PC_In(id_rr_buffer_1_pc_out), .Clk_FBuff(Clock));  // open: Rx_Out, ALU_Out, Dest_Out, Opcode_Out, PC_Out
  PC pc_2 ();  // open: Din, Dout, Clk, Clear_PC
  // also tied to GND on the sheet: chk_z

  // Notes on the sheet:
  //   FETCH
  //   Counter
  //   Imm B15-B0
  //   Rs_B B15-B12
  //   Rs_A B19-B16
  //   Rd
  //   B23-B20
  //   Unused
  //   B25-B24
  //   Opcode B31-B26
  //   Imm
  //   Rs_B
  //   Rs_A
  //   Rd
  //   OpCode
  //   PC
  //   Sign Extend
  //   ID/RR
  //   Dest
  //   Data_R2
  //   Dest
  //   Opcode
  //   PC
  //   EX
  //   Data_R1
endmodule

module PC (
  input  [31:0] Din,
  input  Clk,
  input  Clear_PC,
  output [31:0] Dout
);

  Register #(.width(32)) PC (.D(Din), .Q(Dout), .clk(Clk), .clr(Clear_PC));  // open: en
endmodule

// I-MEM
module Instruction_Memory (
  input  [31:0] Din,
  input  Clk,
  input  Clear_IR,
  output [31:0] Dout
);

  RAM #(.addrWidth(24), .dataWidth(32)) ram_1 (
    .addr(Din[23:0]), .data(Dout), .clk(Clk), .ld(1'b1), .clr(Clear_IR));  // open: sel
endmodule

module _1 (
  input  [31:0] Din,
  output [31:0] Dout
);

  Adder #(.width(32)) adder_1 (.a(Din), .b(32'h1), .out(Dout));  // open: cin, cout
endmodule

// FETCH\nBUFFER
module Fetch_Buffer (
  input  [15:0] Offset_In,
  input  [3:0] Rs_B_In,
  input  [3:0] Rs_A_In,
  input  [3:0] Rd_In,
  input  [5:0] OpCode_In,
  input  [31:0] PC_In,
  input  Clk_FBuff,
  output [15:0] Offset_Out,
  output [3:0] Rs_B_Out,
  output [3:0] Rs_A_Out,
  output [3:0] Rd_Out,
  output [5:0] Opcode_Out,
  output [31:0] PC_Out
);

  Register #(.width(16)) register_1 (.D(Offset_In), .Q(Offset_Out), .clk(Clk_FBuff));  // open: en, clr
  Register #(.width(4)) register_2 (.D(Rs_B_In), .Q(Rs_B_Out), .clk(Clk_FBuff));  // open: en, clr
  Register #(.width(4)) register_3 (.D(Rs_A_In), .Q(Rs_A_Out), .clk(Clk_FBuff));  // open: en, clr
  Register #(.width(4)) register_4 (.D(Rd_In), .Q(Rd_Out), .clk(Clk_FBuff));  // open: en, clr
  Register #(.width(6)) register_5 (.D(OpCode_In), .Q(Opcode_Out), .clk(Clk_FBuff));  // open: en, clr
  Register #(.width(32)) register_6 (.D(PC_In), .Q(PC_Out), .clk(Clk_FBuff));  // open: en, clr
endmodule

// ID/RR\nBUFFER
module ID_RR_Buffer (
  input  [31:0] Offset_In,
  input  [31:0] Data_R1_In,
  input  [31:0] Data_R2_In,
  input  [3:0] Dest_In,
  input  [5:0] OpCode_In,
  input  [31:0] PC_In,
  input  Clk_FBuff,
  output [31:0] Offset_Out,
  output [31:0] Data_R1_Out,
  output [31:0] Data_R2_Out,
  output [3:0] Dest_Out,
  output [5:0] Opcode_Out,
  output [31:0] PC_Out
);

  Register #(.width(32)) register_1 (.D(Offset_In), .Q(Offset_Out), .clk(Clk_FBuff));  // open: en, clr
  Register #(.width(32)) register_2 (.D(Data_R1_In), .Q(Data_R1_Out), .clk(Clk_FBuff));  // open: en, clr
  Register #(.width(32)) register_3 (.D(Data_R2_In), .Q(Data_R2_Out), .clk(Clk_FBuff));  // open: en, clr
  Register #(.width(4)) register_4 (.D(Dest_In), .Q(Dest_Out), .clk(Clk_FBuff));  // open: en, clr
  Register #(.width(6)) register_5 (.D(OpCode_In), .Q(Opcode_Out), .clk(Clk_FBuff));  // open: en, clr
  Register #(.width(32)) register_6 (.D(PC_In), .Q(PC_Out), .clk(Clk_FBuff));  // open: en, clr
endmodule

// ALU\nMain
module ALU_Main (
  input  [31:0] A_In,
  input  [31:0] B_In,
  input  [1:0] FUNC,
  output [31:0] ALU_out
);

  wire [31:0] adder_1_out, nand_1_out, subtractor_1_out;

  Adder #(.width(32)) adder_1 (.a(A_In), .b(B_In), .out(adder_1_out));  // open: cin, cout
  assign nand_1_out = ~(A_In & B_In);  // NAND_Gate nand_1, 32 bits wide
  Multiplexer #(.select(2), .width(32), .enable("false")) multiplexer_1 (
    .in0(adder_1_out), .in1(nand_1_out), .in2(subtractor_1_out), .in3(A_In), .out(ALU_out), .sel(FUNC));
  Subtractor #(.width(32)) subtractor_1 (.a(A_In), .b(B_In), .out(subtractor_1_out));  // open: bin, bout
endmodule

// EX\nBUFFER
module EX_Buffer (
  input  [31:0] Rx_In,
  input  [31:0] ALU_In,
  input  [3:0] Dest_In,
  input  [5:0] OpCode_In,
  input  [31:0] PC_In,
  input  Clk_FBuff,
  output [31:0] Rx_Out,
  output [31:0] ALU_Out,
  output [3:0] Dest_Out,
  output [5:0] Opcode_Out,
  output [31:0] PC_Out
);

  Register #(.width(32)) register_1 (.D(Rx_In), .Q(Rx_Out), .clk(Clk_FBuff));  // open: en, clr
  Register #(.width(32)) register_2 (.D(ALU_In), .Q(ALU_Out), .clk(Clk_FBuff));  // open: en, clr
  Register #(.width(4)) register_3 (.D(Dest_In), .Q(Dest_Out), .clk(Clk_FBuff));  // open: en, clr
  Register #(.width(6)) register_4 (.D(OpCode_In), .Q(Opcode_Out), .clk(Clk_FBuff));  // open: en, clr
  Register #(.width(32)) register_5 (.D(PC_In), .Q(PC_Out), .clk(Clk_FBuff));  // open: en, clr
endmodule
